# Fritzing sketch UROV 2016 wiring (saved by Fritzing 0.9.2b)
breadboards: 2

parts:
  Part1 = Arduino Mega 2560 (Rev3)
  Part2 = Arduino Mega 2560 (Rev3)
  Part3 = 9 Degrees of Freedom - Sensor Stick  # not connected
  U1 = MAX485 [package=dil08]  # not connected
  MD09B1 = A4988 Stepper Motor Driver Carrier
  Power_plug1 = Power plug
  Pressure_sensor = IC, DIP package, 8 pins [chip_label=Pressure]
  J1 = Basic Servo
  J2 = Basic Servo
  J3 = Basic Servo
  J4 = Basic Servo
  J5 = Basic Servo
  J6 = Basic Servo

nets:
  VCC: Part1.AREF, J1.vcc, J2.vcc, J3.vcc, J4.vcc, J5.vcc, J6.vcc
  GND: Part1.GND, Part2.GND, MD09B1.GROUND#141, Power_plug1.GND, Pressure_sensor.pin5, Pressure_sensor.pin6, Pressure_sensor.pin7, Pressure_sensor.pin8, J1.gnd, J2.gnd, J3.gnd, J4.gnd, J5.gnd, J6.gnd
  N1: Part1.D13_PWM, J1.pulse
  N2: Part1.D12_PWM, J2.pulse
  N3: Part1.D11_PWM, J3.pulse
  N4: Part1.D10_PWM, J4.pulse
  N5: Part1.D9_PWM, J6.pulse
  N6: Part1.D8_PWM, J5.pulse
  VIN: Part1.VIN, Part2.VIN, MD09B1.VMOT, Power_plug1.VCC
